# Fritzing sketch Processing2Arduino_Firmata (saved by Fritzing 0.9.3b)
breadboards: 1

parts:
  Part1 = Arduino Uno (Rev3)
  S1 = Pushbutton [package="[THT]"]
  R1 = Resistor [tolerance=±5% resistance=1k package=THT]
  LED1 = LED - 5mm [color="Red (633nm)" package="5 mm [THT]"]
  R2 = Resistor [tolerance=±5% resistance=220 package=THT]

nets:
  N1: Part1.D2, S1.Pin_3, S1.Pin_4, R1.Pin_1
  N2: Part1.D3_PWM, R2.Pin_1
  N3: Part1.5V, R1.Pin_0
  N4: Part1.GND, S1.Pin_1, S1.Pin_2, LED1.cathode
  N5: LED1.anode, R2.Pin_0
