# Fritzing sketch testSerial (saved by Fritzing 0.9.3b)
breadboards: 1

parts:
  Part1 = Arduino Uno (Rev3)
  R1 = Resistor [tolerance=±5% resistance=1k package=THT]
  S1 = Pushbutton [package="[THT]"]
  LED1 = LED - 5mm [color="Red (633nm)" package="5 mm [THT]"]
  R3 = Rotary Potentiometer (Small) [maximum_resistance=100kΩ package=THT]
  R4 = Resistor [tolerance=±5% resistance=220 package=THT]

nets:
  N1: Part1.A0, R3.wiper
  N2: Part1.D13/SCK, LED1.anode
  N3: Part1.D7, R1.Pin_1, S1.Pin_3, S1.Pin_4
  N4: Part1.5V, R1.Pin_0, R3.leg2
  N5: Part1.GND, S1.Pin_1, S1.Pin_2, R3.leg1, R4.Pin_1
  N6: LED1.cathode, R4.Pin_0
